# Fritzing sketch EL-wire Digital Switch (saved by Fritzing 0.8.7b)
circuit board: 2.70459cm x 3.1985cm
breadboards: 1

parts:
  R1 = Resistor [tolerance=±5% resistance=220 package=THT]
  JP2 = Header 2 [package=jst-2-pth-ns]
  R2 = Resistor [tolerance=±5% resistance=150 package=THT]
  JP1 = Header 2 [package=jst-2-pth-ns]
  U1 = MOC3023 [package=dil06]
  JP3 = Header 2 [package=jst-2-pth-ns]
  U2 = TRIAC [package=to-92]  # not connected

nets:
  N1: R1.Pin_0, U1.6
  N2: R1.Pin_1, JP1.2
  N3: JP2.1, JP1.1
  N4: R2.Pin_0, U1.2
  N5: R2.Pin_1, JP3.1
  N6: U1.1, JP3.2

notes:
  el wire power input
  el wire output
  arduino control lines

custom parts:
  MOC3023: Opto-isolated TRIAC
